# Fritzing sketch main (saved by Fritzing 0.9.3b)
breadboards: 1

parts:
  U1 = Carte NUCLEO H755ZI-Q
  R1 = Photocell (LDR) [package=THT]
  R2 = Resistor [tolerance=±5% resistance=10k package=THT]
  Keypad4x1 = Keypad Membran 4x4  # not connected

nets:
  N1: U1.5V, R1.pin_0
  N2: R1.pin_1, R2.Pin_0

custom parts:
  Carte NUCLEO H755ZI-Q: Carte prototype double coeurs ARM
  Keypad Membran 4x4: Membrane Keypad 4x4 Matrix
